// Logisim project Lab 2.circ as structural Verilog
module _2Mux (
  input  A,
  input  S,
  input  B,
  output Out
);

  wire and_1_out, and_2_out, not_1_out;

  not not_1 (not_1_out, S);
  and and_1 (and_1_out, A, not_1_out);
  and and_2 (and_2_out, S, B);
  or or_1 (Out, and_1_out, and_2_out);
endmodule

module Half_Adder (
  input  A,
  input  B,
  output Sum,
  output Carry_Out
);

  wire and_1_out, and_2_out, not_1_out, not_2_out;

  not not_1 (not_1_out, B);
  not not_2 (not_2_out, A);
  and and_1 (and_1_out, A, not_1_out);
  and and_2 (and_2_out, B, not_2_out);
  and and_3 (Carry_Out, A, B);
  or or_1 (Sum, and_1_out, and_2_out);
endmodule

module Full_Adder (
  input  Carry_In,
  input  A,
  input  B,
  output Sum,
  output Carry_Out
);

  wire half_adder_1_carry_out, half_adder_1_sum, half_adder_2_carry_out;

  Half_Adder half_adder_1 (.A(A), .B(B), .Sum(half_adder_1_sum), .Carry_Out(half_adder_1_carry_out));
  Half_Adder half_adder_2 (.A(Carry_In), .B(half_adder_1_sum), .Sum(Sum), .Carry_Out(half_adder_2_carry_out));
  or or_1 (Carry_Out, half_adder_2_carry_out, half_adder_1_carry_out);
endmodule

module _4Mux (
  input  A,
  input  B,
  input  C,
  input  D,
  input  C_1,
  input  C_0,
  output out_7
);

  wire n2mux_1_out, n2mux_2_out;

  _2Mux u_2mux_1 (.A(A), .S(C_0), .B(B), .Out(n2mux_1_out));
  _2Mux u_2mux_2 (.A(C), .S(C_0), .B(D), .Out(n2mux_2_out));
  _2Mux u_2mux_3 (.A(n2mux_1_out), .S(C_1), .B(n2mux_2_out), .Out(out_7));
endmodule

module _1_Bit_ALU (
  input  Carry_In,
  input  A,
  input  B,
  input  C_1,
  input  C_0,
  output Sum,
  output Carry_Out
);

  wire and_1_out, and_2_out, full_adder_1_sum, n2mux_1_out, not_1_out, or_1_out;

  not not_1 (not_1_out, B);
  _2Mux u_2mux_1 (.A(B), .S(and_1_out), .B(not_1_out), .Out(n2mux_1_out));
  and and_1 (and_1_out, C_1, C_0);
  and and_2 (and_2_out, A, B);
  or or_1 (or_1_out, A, B);
  Full_Adder full_adder_1 (.Carry_In(Carry_In), .A(A), .B(n2mux_1_out), .Sum(full_adder_1_sum), .Carry_Out(Carry_Out));
  _4Mux u_4mux_1 (
    .A(full_adder_1_sum), .B(and_2_out), .C(or_1_out), .D(full_adder_1_sum), .C_1(C_1), .C_0(C_0), .out_7(Sum));
endmodule

module _4_Bit_Ripple (
  input  [3:0] A,
  input  [3:0] B,
  input  C_1,
  input  C_0,
  output [3:0] Sum,
  output Carry_Out
);

  wire and_1_out, n1_bit_alu_1_carry_out, n1_bit_alu_2_carry_out, n1_bit_alu_3_carry_out;

  and and_1 (and_1_out, C_0, C_1);
  _1_Bit_ALU u_1_bit_alu_1 (
    .Carry_In(and_1_out), .A(A[0]), .B(B[0]), .C_1(C_1), .C_0(C_0), .Sum(Sum[0]),
    .Carry_Out(n1_bit_alu_1_carry_out));
  _1_Bit_ALU u_1_bit_alu_2 (
    .Carry_In(n1_bit_alu_1_carry_out), .A(A[1]), .B(B[1]), .C_1(C_1), .C_0(C_0), .Sum(Sum[1]),
    .Carry_Out(n1_bit_alu_2_carry_out));
  _1_Bit_ALU u_1_bit_alu_3 (
    .Carry_In(n1_bit_alu_2_carry_out), .A(A[2]), .B(B[2]), .C_1(C_1), .C_0(C_0), .Sum(Sum[2]),
    .Carry_Out(n1_bit_alu_3_carry_out));
  _1_Bit_ALU u_1_bit_alu_4 (
    .Carry_In(n1_bit_alu_3_carry_out), .A(A[3]), .B(B[3]), .C_1(C_1), .C_0(C_0), .Sum(Sum[3]),
    .Carry_Out(Carry_Out));
endmodule

module Full_4_Bit_ALU (
  input  [3:0] A,
  input  [3:0] B,
  input  C_1,
  input  C_0,
  output [3:0] Sum,
  output Carry_Out
);

  wire and_1_out, n1_bit_alu_1_carry_out, n1_bit_alu_2_carry_out, n1_bit_alu_3_carry_out;

  and and_1 (and_1_out, C_0, C_1);
  _1_Bit_ALU u_1_bit_alu_1 (
    .Carry_In(and_1_out), .A(A[0]), .B(B[0]), .C_1(C_1), .C_0(C_0), .Sum(Sum[0]),
    .Carry_Out(n1_bit_alu_1_carry_out));
  _1_Bit_ALU u_1_bit_alu_2 (
    .Carry_In(n1_bit_alu_1_carry_out), .A(A[1]), .B(B[1]), .C_1(C_1), .C_0(C_0), .Sum(Sum[1]),
    .Carry_Out(n1_bit_alu_2_carry_out));
  _1_Bit_ALU u_1_bit_alu_3 (
    .Carry_In(n1_bit_alu_2_carry_out), .A(A[2]), .B(B[2]), .C_1(C_1), .C_0(C_0), .Sum(Sum[2]),
    .Carry_Out(n1_bit_alu_3_carry_out));
  _1_Bit_ALU u_1_bit_alu_4 (
    .Carry_In(n1_bit_alu_3_carry_out), .A(A[3]), .B(B[3]), .C_1(C_1), .C_0(C_0), .Sum(Sum[3]),
    .Carry_Out(Carry_Out));
endmodule
