// Logisim project Lab 3.circ as structural Verilog
module _2Mux (
  input  A,
  input  S,
  input  B,
  output Out
);

  wire and_1_out, and_2_out, not_1_out;

  not not_1 (not_1_out, S);
  and and_1 (and_1_out, A, not_1_out);
  and and_2 (and_2_out, S, B);
  or or_1 (Out, and_1_out, and_2_out);
endmodule

module Half_Adder (
  input  A,
  input  B,
  output Sum,
  output Carry_Out
);

  wire and_1_out, and_2_out, not_1_out, not_2_out;

  not not_1 (not_1_out, B);
  not not_2 (not_2_out, A);
  and and_1 (and_1_out, A, not_1_out);
  and and_2 (and_2_out, B, not_2_out);
  and and_3 (Carry_Out, A, B);
  or or_1 (Sum, and_1_out, and_2_out);
endmodule

module Full_Adder (
  input  Carry_In,
  input  A,
  input  B,
  output Sum,
  output Carry_Out
);

  wire half_adder_1_carry_out, half_adder_1_sum, half_adder_2_carry_out;

  Half_Adder half_adder_1 (.A(A), .B(B), .Sum(half_adder_1_sum), .Carry_Out(half_adder_1_carry_out));
  Half_Adder half_adder_2 (.A(Carry_In), .B(half_adder_1_sum), .Sum(Sum), .Carry_Out(half_adder_2_carry_out));
  or or_1 (Carry_Out, half_adder_2_carry_out, half_adder_1_carry_out);
endmodule

module _4Mux (
  input  A,
  input  B,
  input  C,
  input  D,
  input  C_1,
  input  C_0,
  output out_7
);

  wire n2mux_1_out, n2mux_2_out;

  _2Mux u_2mux_1 (.A(A), .S(C_0), .B(B), .Out(n2mux_1_out));
  _2Mux u_2mux_2 (.A(C), .S(C_0), .B(D), .Out(n2mux_2_out));
  _2Mux u_2mux_3 (.A(n2mux_1_out), .S(C_1), .B(n2mux_2_out), .Out(out_7));
endmodule

module _1_Bit_ALU (
  input  Carry_In,
  input  A,
  input  B,
  input  C_1,
  input  C_0,
  output Sum,
  output Carry_Out
);

  wire and_1_out, and_2_out, full_adder_1_sum, n2mux_1_out, not_1_out, or_1_out;

  not not_1 (not_1_out, B);
  _2Mux u_2mux_1 (.A(B), .S(and_1_out), .B(not_1_out), .Out(n2mux_1_out));
  and and_1 (and_1_out, C_1, C_0);
  and and_2 (and_2_out, A, B);
  or or_1 (or_1_out, A, B);
  Full_Adder full_adder_1 (.Carry_In(Carry_In), .A(A), .B(n2mux_1_out), .Sum(full_adder_1_sum), .Carry_Out(Carry_Out));
  _4Mux u_4mux_1 (
    .A(full_adder_1_sum), .B(and_2_out), .C(or_1_out), .D(full_adder_1_sum), .C_1(C_1), .C_0(C_0), .out_7(Sum));
endmodule

module _4_Bit_Ripple (
  input  [3:0] A,
  input  [3:0] B,
  input  C_1,
  input  C_0,
  output [3:0] Sum,
  output Carry_Out
);

  wire and_1_out, n1_bit_alu_1_carry_out, n1_bit_alu_2_carry_out, n1_bit_alu_3_carry_out;

  and and_1 (and_1_out, C_0, C_1);
  _1_Bit_ALU u_1_bit_alu_1 (
    .Carry_In(and_1_out), .A(A[0]), .B(B[0]), .C_1(C_1), .C_0(C_0), .Sum(Sum[0]),
    .Carry_Out(n1_bit_alu_1_carry_out));
  _1_Bit_ALU u_1_bit_alu_2 (
    .Carry_In(n1_bit_alu_1_carry_out), .A(A[1]), .B(B[1]), .C_1(C_1), .C_0(C_0), .Sum(Sum[1]),
    .Carry_Out(n1_bit_alu_2_carry_out));
  _1_Bit_ALU u_1_bit_alu_3 (
    .Carry_In(n1_bit_alu_2_carry_out), .A(A[2]), .B(B[2]), .C_1(C_1), .C_0(C_0), .Sum(Sum[2]),
    .Carry_Out(n1_bit_alu_3_carry_out));
  _1_Bit_ALU u_1_bit_alu_4 (
    .Carry_In(n1_bit_alu_3_carry_out), .A(A[3]), .B(B[3]), .C_1(C_1), .C_0(C_0), .Sum(Sum[3]),
    .Carry_Out(Carry_Out));
endmodule

module Full_4_Bit_ALU (
  input  [3:0] A,
  input  [3:0] B,
  input  S_1,
  input  S_0,
  output [3:0] Sum,
  output Carry_Out
);

  wire and_1_out, n1_bit_alu_1_carry_out, n1_bit_alu_2_carry_out, n1_bit_alu_3_carry_out;

  and and_1 (and_1_out, S_0, S_1);
  _1_Bit_ALU u_1_bit_alu_1 (
    .Carry_In(and_1_out), .A(A[0]), .B(B[0]), .C_1(S_1), .C_0(S_0), .Sum(Sum[0]),
    .Carry_Out(n1_bit_alu_1_carry_out));
  _1_Bit_ALU u_1_bit_alu_2 (
    .Carry_In(n1_bit_alu_1_carry_out), .A(A[1]), .B(B[1]), .C_1(S_1), .C_0(S_0), .Sum(Sum[1]),
    .Carry_Out(n1_bit_alu_2_carry_out));
  _1_Bit_ALU u_1_bit_alu_3 (
    .Carry_In(n1_bit_alu_2_carry_out), .A(A[2]), .B(B[2]), .C_1(S_1), .C_0(S_0), .Sum(Sum[2]),
    .Carry_Out(n1_bit_alu_3_carry_out));
  _1_Bit_ALU u_1_bit_alu_4 (
    .Carry_In(n1_bit_alu_3_carry_out), .A(A[3]), .B(B[3]), .C_1(S_1), .C_0(S_0), .Sum(Sum[3]),
    .Carry_Out(Carry_Out));
endmodule

module D_Register (
  input  [3:0] Data_In,
  input  CLK,
  input  WE,
  output [3:0] Data_Out
);

  D_Flip_Flop d_ff_1 (.clk(CLK), .D(Data_In[0]), .Q(Data_Out[0]), .en(WE));  // open: Qn, preset, reset
  D_Flip_Flop d_ff_2 (.clk(CLK), .D(Data_In[1]), .Q(Data_Out[1]), .en(WE));  // open: Qn, preset, reset
  D_Flip_Flop d_ff_3 (.clk(CLK), .D(Data_In[2]), .Q(Data_Out[2]), .en(WE));  // open: Qn, preset, reset
  D_Flip_Flop d_ff_4 (.clk(CLK), .D(Data_In[3]), .Q(Data_Out[3]), .en(WE));  // open: Qn, preset, reset
endmodule

module Register_File (
  input  [2:0] RA2,
  input  [2:0] RA1,
  input  [3:0] Data_In,
  input  [2:0] WA,
  input  CLK,
  input  WE,
  output [3:0] Out1,
  output [3:0] Out1_2
);

  wire demultiplexer_2_out0, demultiplexer_2_out1, demultiplexer_2_out2, demultiplexer_2_out3,
       demultiplexer_2_out4, demultiplexer_2_out5, demultiplexer_2_out6, demultiplexer_2_out7;
  wire [3:0] d_register_1_data_out, d_register_2_data_out, d_register_3_data_out, d_register_4_data_out,
       d_register_5_data_out, d_register_6_data_out, d_register_7_data_out, d_register_8_data_out,
       demultiplexer_1_out0, demultiplexer_1_out1, demultiplexer_1_out2, demultiplexer_1_out3,
       demultiplexer_1_out4, demultiplexer_1_out5, demultiplexer_1_out6, demultiplexer_1_out7;

  Demultiplexer #(.select(3), .width(4), .enable("false")) demultiplexer_1 (
    .out0(demultiplexer_1_out0), .out1(demultiplexer_1_out1), .out2(demultiplexer_1_out2),
    .out3(demultiplexer_1_out3), .out4(demultiplexer_1_out4), .out5(demultiplexer_1_out5),
    .out6(demultiplexer_1_out6), .out7(demultiplexer_1_out7), .in(Data_In), .sel(WA));
  D_Register d_register_1 (
    .Data_In(demultiplexer_1_out0), .CLK(CLK), .WE(demultiplexer_2_out0), .Data_Out(d_register_1_data_out));
  D_Register d_register_2 (
    .Data_In(demultiplexer_1_out1), .CLK(CLK), .WE(demultiplexer_2_out1), .Data_Out(d_register_2_data_out));
  D_Register d_register_3 (
    .Data_In(demultiplexer_1_out2), .CLK(CLK), .WE(demultiplexer_2_out2), .Data_Out(d_register_3_data_out));
  D_Register d_register_4 (
    .Data_In(demultiplexer_1_out3), .CLK(CLK), .WE(demultiplexer_2_out3), .Data_Out(d_register_4_data_out));
  D_Register d_register_5 (
    .Data_In(demultiplexer_1_out4), .CLK(CLK), .WE(demultiplexer_2_out4), .Data_Out(d_register_5_data_out));
  D_Register d_register_6 (
    .Data_In(demultiplexer_1_out5), .CLK(CLK), .WE(demultiplexer_2_out5), .Data_Out(d_register_6_data_out));
  D_Register d_register_7 (
    .Data_In(demultiplexer_1_out6), .CLK(CLK), .WE(demultiplexer_2_out6), .Data_Out(d_register_7_data_out));
  D_Register d_register_8 (
    .Data_In(demultiplexer_1_out7), .CLK(CLK), .WE(demultiplexer_2_out7), .Data_Out(d_register_8_data_out));
  Demultiplexer #(.select(3), .enable("false")) demultiplexer_2 (
    .out0(demultiplexer_2_out0), .out1(demultiplexer_2_out1), .out2(demultiplexer_2_out2),
    .out3(demultiplexer_2_out3), .out4(demultiplexer_2_out4), .out5(demultiplexer_2_out5),
    .out6(demultiplexer_2_out6), .out7(demultiplexer_2_out7), .in(WE), .sel(WA));
  Multiplexer #(.select(3), .width(4), .enable("false")) multiplexer_1 (
    .in0(d_register_1_data_out), .in1(d_register_2_data_out), .in2(d_register_3_data_out),
    .in3(d_register_4_data_out), .in4(d_register_5_data_out), .in5(d_register_6_data_out),
    .in6(d_register_7_data_out), .in7(d_register_8_data_out), .out(Out1), .sel(RA1));
  Multiplexer #(.select(3), .width(4), .enable("false")) multiplexer_2 (
    .in0(d_register_1_data_out), .in1(d_register_2_data_out), .in2(d_register_3_data_out),
    .in3(d_register_4_data_out), .in4(d_register_5_data_out), .in5(d_register_6_data_out),
    .in6(d_register_7_data_out), .in7(d_register_8_data_out), .out(Out1_2), .sel(RA2));
endmodule

module Register___ALU (
  input  CLK,
  input  WE,
  input  [11:0] Input_Word,
  output [3:0] out_4,
  output out_5
);

  wire [3:0] bit_extender_1_out, multiplexer_1_out, register_file_1_out1, register_file_1_out1_2;

  Register_File register_file_1 (
    .Data_In(out_4), .WA(Input_Word[8:6]), .CLK(CLK), .WE(WE), .RA2(Input_Word[2:0]), .RA1(Input_Word[5:3]),
    .Out1(register_file_1_out1), .Out1_2(register_file_1_out1_2));
  assign bit_extender_1_out = {{1{Input_Word[2]}}, Input_Word[2:0]};  // Bit_Extender bit_extender_1
  Multiplexer #(.width(4), .enable("false")) multiplexer_1 (
    .in0(register_file_1_out1_2), .in1(bit_extender_1_out), .out(multiplexer_1_out), .sel(Input_Word[11]));
  Full_4_Bit_ALU full_4_bit_alu_1 (
    .A(register_file_1_out1), .B(multiplexer_1_out), .S_1(Input_Word[10]), .S_0(Input_Word[9]), .Sum(out_4),
    .Carry_Out(out_5));
endmodule
